# Fritzing sketch photoresistor (saved by Fritzing 0.9.3b)
breadboards: 1

parts:
  IC1 = MCP3008 8-channel 10-bit ADC [part_number=MCP3008]
  Part1 = Adafruit T-Cobbler Plus [part_number="Adafruit #1989 and #2028"]
  R1 = Resistor [tolerance=±5% resistance=10k package=THT]
  LED2 = smd LED [color="White (8000K)" package="0603 [SMD]"]
  R2 = Resistor [tolerance=±5% resistance=100k package=THT]
  R3 = PHOTOCELL [package=photocell]

nets:
  N1: IC1.no_name_yet#1, R2.Pin_1, R3.P$1
  N2: IC1.no_name_yet#2, R1.Pin_1, LED2.anode
  N3: IC1.no_name_yet#9, IC1.no_name_yet#14, Part1.GND, LED2.cathode, R3.P$2
  N4: IC1.no_name_yet#10, Part1.GPIO5
  N5: IC1.no_name_yet#11, Part1.SCLK
  N6: IC1.no_name_yet#12, Part1.MOSI
  N7: IC1.no_name_yet#13, Part1.MISO
  N8: IC1.no_name_yet#15, IC1.no_name_yet#16, Part1.+3.3V, R2.Pin_0
  N9: Part1.TXD, R1.Pin_0

custom parts:
  Adafruit T-Cobbler Plus: The Raspberry Pi has landed on the Maker World like a 40-GPIO pinned, quad-USB ported, credit card sized bomb of DIY joy. And while you can use most of our great Model B accessories by hooking up our downgrade cable, its probably a good time to upgrade your set up and accessorize using all of the 40 pins. That's why we now carry the Assembled Adafruit Pi T-Cobbler Plus - Breakout + Cable for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
